// Logisim project SPIM.circ as structural Verilog: 3 circuits, main circuit Processador
module Banco_Reg_af421015 (
  input  Clock,
  input  [15:0] C,
  input  Write,
  input  [2:0] c_2,
  input  [2:0] A,
  input  [2:0] B,
  output [15:0] a_2,
  output [15:0] b_2
);

  wire demultiplexer_1_out1, demultiplexer_1_out2, demultiplexer_1_out3, demultiplexer_1_out4,
       demultiplexer_1_out5, demultiplexer_1_out6, demultiplexer_1_out7;
  wire [15:0] register_1_q, register_2_q, register_3_q, register_4_q, register_5_q, register_6_q,
       register_7_q, register_8_q;

  Demultiplexer #(.select(3), .enable("false")) demultiplexer_1 (
    .out1(demultiplexer_1_out1), .out2(demultiplexer_1_out2), .out3(demultiplexer_1_out3),
    .out4(demultiplexer_1_out4), .out5(demultiplexer_1_out5), .out6(demultiplexer_1_out6),
    .out7(demultiplexer_1_out7), .in(Write), .sel(c_2));  // open: out0
  Register #(.width(16)) register_1 (.D(C), .en(1'b0), .Q(register_1_q), .clk(Clock), .clr(1'b1));
  Register #(.width(16)) register_2 (.D(C), .en(demultiplexer_1_out1), .Q(register_2_q), .clk(Clock));  // open: clr
  Register #(.width(16)) register_3 (.D(C), .en(demultiplexer_1_out2), .Q(register_3_q), .clk(Clock));  // open: clr
  Register #(.width(16)) register_4 (.D(C), .en(demultiplexer_1_out3), .Q(register_4_q), .clk(Clock));  // open: clr
  Register #(.width(16)) register_5 (.D(C), .en(demultiplexer_1_out4), .Q(register_5_q), .clk(Clock), .clr(Clock));
  Register #(.width(16)) register_6 (.D(C), .en(demultiplexer_1_out5), .Q(register_6_q), .clk(Clock));  // open: clr
  Register #(.width(16)) register_7 (.D(C), .en(demultiplexer_1_out6), .Q(register_7_q), .clk(Clock));  // open: clr
  Register #(.width(16)) register_8 (.D(C), .en(demultiplexer_1_out7), .Q(register_8_q), .clk(Clock));  // open: clr
  Multiplexer #(.select(3), .width(16)) multiplexer_1 (
    .in0(register_1_q), .in1(register_2_q), .in2(register_3_q), .in3(register_4_q), .in4(register_5_q),
    .in5(register_6_q), .in6(register_7_q), .in7(register_8_q), .out(a_2), .sel(A));  // open: en
  Multiplexer #(.select(3), .width(16)) multiplexer_2 (
    .in0(register_1_q), .in1(register_2_q), .in2(register_3_q), .in3(register_4_q), .in4(register_5_q),
    .in5(register_6_q), .in6(register_7_q), .in7(register_8_q), .out(b_2), .sel(B));  // open: en
endmodule

module Ula (
  input  [15:0] A,
  input  [15:0] B,
  input  in_3,
  input  [1:0] ULASel,
  input  CompSel,
  output [15:0] \Saída ,
  output out_7,
  output out_8,
  output Comparador
);

  wire comparator_1_eq, comparator_1_lt;
  wire [3:0] bit_extender_1_out;
  wire [15:0] adder_1_out, shifter_1_out, subtractor_1_out;

  Bit_Extender #(.in_width(16), .out_width(4)) bit_extender_1 (.in(A), .out(bit_extender_1_out));
  Adder #(.width(16)) adder_1 (.a(B), .b(A), .out(adder_1_out), .cin(in_3), .cout(out_7));
  Subtractor #(.width(16)) subtractor_1 (.a(B), .b(A), .out(subtractor_1_out), .bin(in_3), .bout(out_8));
  Shifter #(.width(16)) shifter_1 (.in(B), .\dist (bit_extender_1_out), .out(shifter_1_out));
  Comparator #(.width(16)) comparator_1 (.a(B), .b(A), .eq(comparator_1_eq), .lt(comparator_1_lt));  // open: gt
  Multiplexer #(.enable("false")) multiplexer_1 (
    .in0(comparator_1_eq), .in1(comparator_1_lt), .out(Comparador), .sel(CompSel));
  Multiplexer #(.select(2), .width(16), .enable("false")) multiplexer_2 (
    .in0(adder_1_out), .in1(subtractor_1_out), .in2(shifter_1_out), .out(\Saída ), .sel(ULASel));  // open: in3
endmodule

module Processador (
  input  Reset,
  output [15:0] out_2,
  output Sel_Reg,
  output Comp__Sel,
  output [1:0] ULA_OP,
  output Mem_Read,
  output Mem_Write,
  output Sel_Data,
  output Sel_B,
  output Reg_Write,
  output [1:0] Sel_IP
);

  wire and_1_out, clock_1_out, ULA_comparador;
  wire [2:0] multiplexer_3_out;
  wire [3:0] rom_1_data;
  wire [5:0] adder_1_out, multiplexer_1_out, multiplexer_2_out, PC_q;
  wire [11:0] rom_1_data_2;
  wire [15:0] bit_extender_1_out, multiplexer_4_out, multiplexer_5_out, ram_1_data, Registradores_a_2,
       Registradores_b_2;

  Clock clock_1 (.out(clock_1_out));
  Multiplexer #(.width(6), .enable("false")) multiplexer_1 (
    .in0(adder_1_out), .in1(rom_1_data_2[5:0]), .out(multiplexer_1_out), .sel(and_1_out));
  Multiplexer #(.select(2), .width(6), .enable("false")) multiplexer_2 (
    .in0(adder_1_out), .in1(rom_1_data_2[5:0]), .in2(multiplexer_1_out), .out(multiplexer_2_out), .sel(Sel_IP));  // open: in3
  Register #(.width(6)) PC (.D(multiplexer_2_out), .Q(PC_q), .clk(clock_1_out), .clr(Reset));  // open: en
  and and_1 (and_1_out, 1'b1, ULA_comparador);
  Adder #(.width(6)) adder_1 (.a(PC_q), .b(6'b000001), .out(adder_1_out));  // open: cin, cout
  ROM #(.addrWidth(6), .dataWidth(16)) rom_1 (.addr(PC_q), .data({rom_1_data, rom_1_data_2}));  // open: sel
  ROM #(.addrWidth(4), .dataWidth(11)) rom_2 (
    .addr(rom_1_data),
    .data({Sel_IP, Reg_Write, Sel_B, Sel_Data, Mem_Write, Mem_Read, ULA_OP, Comp__Sel, Sel_Reg}));  // open: sel
  Multiplexer #(.width(3), .enable("false")) multiplexer_3 (
    .in0(rom_1_data_2[5:3]), .in1(rom_1_data_2[11:9]), .out(multiplexer_3_out), .sel(Sel_Reg));
  Banco_Reg_af421015 Registradores (
    .Clock(clock_1_out), .C(multiplexer_5_out), .Write(Reg_Write), .c_2(rom_1_data_2[11:9]),
    .A(rom_1_data_2[8:6]), .B(multiplexer_3_out), .a_2(Registradores_a_2), .b_2(Registradores_b_2));
  assign bit_extender_1_out = {{10{1'b0}}, rom_1_data_2[5:0]};  // Bit_Extender bit_extender_1
  Multiplexer #(.width(16), .enable("false")) multiplexer_4 (
    .in0(Registradores_b_2), .in1(bit_extender_1_out), .out(multiplexer_4_out), .sel(Sel_B));
  Multiplexer #(.width(16), .enable("false")) multiplexer_5 (
    .in0(ram_1_data), .in1(out_2), .out(multiplexer_5_out), .sel(Sel_Data));
  Ula ULA (
    .A(Registradores_a_2), .B(multiplexer_4_out), .CompSel(Comp__Sel), .ULASel(ULA_OP), .\Saída (out_2),
    .Comparador(ULA_comparador));  // open: in_3, out_7, out_8
  RAM #(.addrWidth(16), .dataWidth(16), .bus("separate")) ram_1 (
    .addr(out_2), .din(Registradores_b_2), .data(ram_1_data), .str(Mem_Write), .sel(1'b1), .clk(clock_1_out),
    .ld(Mem_Read));  // open: clr

  // Other names for the same wires on the sheet: rst = Reset

  // Notes on the sheet:
  //   contents of rom_1 (hex, n*v repeats v):
  //   1400 5480 1200 1a00 1c00 1e01 1601 828e 6ac0 2bb8 1f80 1d40 1241 7007 6ac0
  //   contents of rom_2 (hex, n*v repeats v):
  //   0 1c0 140 144 1c8 190 a1 200 401 142
endmodule
