// Logisim project ula.circ as structural Verilog: 1 circuit, main circuit main
module main (
  input  in_1,
  input  [15:0] A,
  input  [15:0] B,
  input  [1:0] ULASel,
  input  CompSel,
  input  WRITE_DATA_1dadb6f3,
  input  A_2,
  input  B_2,
  input  C,
  input  ENABLE,
  input  in_11,
  input  in_12,
  input  in_13,
  input  in_14,
  input  Enable_2,
  input  S2,
  input  S1,
  input  S0,
  input  in_19,
  input  in_20,
  input  Enable_3,
  input  S2_2,
  input  S1_2,
  input  S0_2,
  input  in_25,
  input  in_26,
  input  in_27,
  input  in_28,
  input  in_29,
  input  in_30,
  input  in_31,
  input  in_32,
  input  in_33,
  input  in_34,
  input  in_35,
  input  in_36,
  input  in_37,
  input  in_38,
  input  in_39,
  input  in_40,
  input  in_41,
  input  in_42,
  input  in_43,
  input  in_44,
  input  in_45,
  input  in_46,
  input  in_47,
  input  in_48,
  input  in_49,
  input  in_50,
  input  in_51,
  input  in_52,
  output [15:0] \Saída ,
  output out_54,
  output out_55,
  output Comparador
);

  wire and_1_out, and_2_out, and_3_out, and_4_out, and_5_out, and_6_out, and_7_out, and_8_out, and_9_out,
       and_10_out, and_11_out, and_12_out, and_13_out, and_14_out, and_15_out, and_16_out, and_17_out,
       and_18_out, and_19_out, and_20_out, and_21_out, and_22_out, and_23_out, and_24_out, and_25_out,
       and_26_out, and_27_out, and_28_out, and_29_out, and_30_out, and_31_out, and_32_out, and_33_out,
       and_34_out, and_35_out, and_36_out, and_37_out, and_38_out, and_39_out, and_40_out, and_41_out,
       and_42_out, and_43_out, and_44_out, and_45_out, and_46_out, and_47_out, and_48_out, and_49_out,
       and_50_out, and_51_out, and_52_out, and_53_out, and_54_out, and_55_out, and_56_out, and_57_out,
       and_58_out, and_59_out, and_60_out, and_61_out, and_62_out, and_63_out, and_64_out, and_65_out,
       and_66_out, and_67_out, and_68_out, and_69_out, and_70_out, and_71_out, and_72_out, and_73_out,
       and_74_out, and_75_out, and_76_out, and_77_out, and_78_out, and_79_out, and_80_out, and_81_out,
       and_82_out, and_83_out, and_84_out, and_85_out, and_86_out, and_87_out, and_88_out, and_89_out,
       and_90_out, and_91_out, and_92_out, and_93_out, and_94_out, and_95_out, and_96_out, and_97_out,
       and_98_out, and_99_out, and_100_out, and_101_out, and_102_out, and_103_out, and_104_out, and_105_out,
       and_106_out, and_107_out, and_108_out, and_109_out, and_110_out, and_111_out, and_112_out,
       and_113_out, and_114_out, and_115_out, and_116_out, and_117_out, and_118_out, and_119_out,
       and_120_out, and_121_out, and_122_out, and_123_out, and_124_out, and_125_out, and_126_out,
       and_127_out, and_128_out, and_129_out, and_130_out, and_131_out, and_132_out, and_133_out,
       and_134_out, and_135_out, and_136_out, and_137_out, and_138_out, and_139_out, and_140_out,
       and_141_out, and_142_out, and_143_out, and_144_out, and_145_out, and_146_out, and_147_out,
       and_148_out, and_149_out, and_150_out, and_151_out, and_152_out, and_153_out, and_154_out,
       and_155_out, and_156_out, and_157_out, and_158_out, and_159_out, and_160_out, and_161_out,
       and_162_out, and_163_out, and_164_out, and_165_out, and_166_out, and_167_out, and_168_out,
       and_169_out, and_170_out, and_171_out, and_172_out, and_173_out, and_174_out, and_175_out,
       and_176_out, and_177_out, and_178_out, and_179_out, and_180_out, and_181_out, and_182_out,
       and_183_out, and_184_out, and_185_out, and_186_out, and_187_out, and_188_out, and_189_out,
       and_190_out, and_191_out, and_192_out, and_193_out, and_194_out, and_195_out, and_196_out,
       and_197_out, and_198_out, and_199_out, and_200_out, and_201_out, and_202_out, and_203_out,
       and_204_out, and_205_out, and_206_out, and_207_out, and_208_out, clock_1_out, comparator_1_eq,
       comparator_1_lt, nand_1_out, nand_2_out, nand_3_out, nand_4_out, nand_5_out, nand_6_out, nand_7_out,
       nand_8_out, nand_9_out, nand_10_out, nand_11_out, nand_12_out, nand_13_out, nand_14_out, nand_15_out,
       nand_16_out, nand_17_out, nand_18_out, nand_19_out, nand_20_out, nand_21_out, nand_22_out,
       nand_23_out, nand_24_out, nand_25_out, nand_26_out, nand_27_out, nand_28_out, nand_29_out,
       nand_30_out, nand_31_out, nand_32_out, nand_33_out, nand_34_out, nand_35_out, nand_36_out,
       nand_37_out, nand_38_out, nand_39_out, nand_40_out, nand_41_out, nand_42_out, nand_43_out,
       nand_44_out, nand_45_out, nand_46_out, nand_47_out, nand_48_out, nor_1_out, nor_2_out, nor_3_out,
       nor_4_out, nor_5_out, nor_6_out, nor_7_out, nor_8_out, nor_9_out, nor_10_out, nor_11_out, nor_12_out,
       nor_13_out, nor_14_out, nor_15_out, nor_16_out, nor_17_out, nor_18_out, not_1_out, not_2_out,
       not_3_out, not_4_out, not_5_out, not_6_out, not_7_out, not_8_out, not_9_out, not_10_out, not_11_out,
       not_12_out, not_13_out, not_14_out, not_15_out, not_16_out, not_17_out, not_18_out, not_19_out,
       not_20_out, not_21_out, not_22_out, not_23_out, not_24_out, not_25_out, not_26_out, not_27_out,
       not_28_out, not_29_out, not_30_out, not_31_out, not_32_out, not_33_out, not_34_out, not_35_out,
       or_1_out, or_2_out, or_3_out, or_4_out, or_5_out, or_6_out, or_7_out, or_8_out, or_9_out, or_10_out,
       or_11_out, or_12_out, or_13_out, or_14_out, or_15_out, or_16_out, or_17_out, or_18_out, or_19_out,
       or_20_out, or_21_out, or_22_out, or_23_out, or_24_out, or_25_out, or_26_out, or_27_out, or_28_out,
       or_29_out, or_30_out, or_31_out, or_32_out, or_33_out, or_34_out, or_35_out, or_36_out, or_37_out,
       or_38_out, or_39_out, or_40_out, or_41_out, or_42_out, or_43_out, or_44_out, or_45_out, or_46_out,
       or_47_out, or_48_out, xor_1_out, xor_2_out, xor_3_out, xor_4_out, xor_5_out, xor_6_out, xor_7_out,
       xor_8_out, xor_9_out, xor_10_out, xor_11_out, xor_12_out, xor_13_out, xor_14_out, xor_15_out,
       xor_16_out, xor_17_out, xor_18_out, xor_19_out, xor_20_out, xor_21_out, xor_22_out, xor_23_out,
       xor_24_out, xor_25_out, xor_26_out, xor_27_out, xor_28_out, xor_29_out, xor_30_out, xor_31_out,
       xor_32_out, xor_33_out, xor_34_out, xor_35_out, xor_36_out, xor_37_out, xor_38_out, xor_39_out,
       xor_40_out, xor_41_out, xor_42_out, xor_43_out, xor_44_out, xor_45_out, xor_46_out, xor_47_out,
       xor_48_out, xor_49_out, xor_50_out, xor_51_out, xor_52_out, xor_53_out, xor_54_out, xor_55_out,
       xor_56_out, xor_57_out, xor_58_out, xor_59_out, xor_60_out, xor_61_out, xor_62_out, xor_63_out,
       xor_64_out;
  wire [3:0] bit_extender_1_out;
  wire [15:0] adder_1_out, shifter_1_out, subtractor_1_out;

  Bit_Extender #(.in_width(16), .out_width(4)) bit_extender_1 (.in(A), .out(bit_extender_1_out));
  Adder #(.width(16)) adder_1 (.a(B), .b(A), .out(adder_1_out), .cin(in_1), .cout(out_54));
  Subtractor #(.width(16)) subtractor_1 (.a(B), .b(A), .out(subtractor_1_out), .bin(in_1), .bout(out_55));
  Shifter #(.width(16)) shifter_1 (.in(B), .\dist (bit_extender_1_out), .out(shifter_1_out));
  Comparator #(.width(16)) comparator_1 (.a(B), .b(A), .eq(comparator_1_eq), .lt(comparator_1_lt));  // open: gt
  Multiplexer #(.enable("false")) multiplexer_1 (
    .in0(comparator_1_eq), .in1(comparator_1_lt), .out(Comparador), .sel(CompSel));
  and and_1 (and_1_out, ~A_2, ~B_2, ~C, ENABLE);  // AND_Gate
  and and_2 (and_2_out, ~A_2, ~B_2, C, ENABLE);  // AND_Gate
  and and_3 (and_3_out, ~A_2, B_2, ~C, ENABLE);  // AND_Gate
  and and_4 (and_4_out, ~A_2, B_2, C, ENABLE);  // AND_Gate
  and and_5 (and_5_out, A_2, ~B_2, ~C, ENABLE);  // AND_Gate
  and and_6 (and_6_out, A_2, ~B_2, C, ENABLE);  // AND_Gate
  and and_7 (and_7_out, A_2, B_2, ~C, ENABLE);  // AND_Gate
  and and_8 (and_8_out, A_2, B_2, C, ENABLE);
  Multiplexer #(.select(2), .width(16), .enable("false")) multiplexer_2 (
    .in0(adder_1_out), .in1(subtractor_1_out), .in2(shifter_1_out), .out(\Saída ), .sel(ULASel));  // open: in3
  Clock clock_1 (.out(clock_1_out));
  and and_9 (and_9_out, and_1_out, clock_1_out);
  not not_1 (not_1_out, WRITE_DATA_1dadb6f3);
  and and_10 (and_10_out, clock_1_out, and_3_out);
  not not_2 (not_2_out, WRITE_DATA_1dadb6f3);
  and and_11 (and_11_out, and_5_out, clock_1_out);
  not not_3 (not_3_out, WRITE_DATA_1dadb6f3);
  and and_12 (and_12_out, clock_1_out, and_7_out);
  not not_4 (not_4_out, WRITE_DATA_1dadb6f3);
  nand nand_1 (nand_1_out, WRITE_DATA_1dadb6f3, and_9_out);
  nand nand_2 (nand_2_out, and_9_out, not_1_out);
  nand nand_3 (nand_3_out, WRITE_DATA_1dadb6f3, and_10_out);
  nand nand_4 (nand_4_out, and_10_out, not_2_out);
  nand nand_5 (nand_5_out, WRITE_DATA_1dadb6f3, and_11_out);
  nand nand_6 (nand_6_out, and_11_out, not_3_out);
  nand nand_7 (nand_7_out, WRITE_DATA_1dadb6f3, and_12_out);
  nand nand_8 (nand_8_out, and_12_out, not_4_out);
  nand nand_9 (nand_9_out, nand_1_out, nand_10_out);
  nand nand_10 (nand_10_out, nand_9_out, nand_2_out);
  nand nand_11 (nand_11_out, nand_3_out, nand_12_out);
  nand nand_12 (nand_12_out, nand_11_out, nand_4_out);
  nand nand_13 (nand_13_out, nand_5_out, nand_14_out);
  nand nand_14 (nand_14_out, nand_13_out, nand_6_out);
  nand nand_15 (nand_15_out, nand_7_out, nand_16_out);
  nand nand_16 (nand_16_out, nand_15_out, nand_8_out);
  and and_13 (and_13_out, and_2_out, clock_1_out);
  not not_5 (not_5_out, WRITE_DATA_1dadb6f3);
  and and_14 (and_14_out, and_4_out, clock_1_out);
  not not_6 (not_6_out, WRITE_DATA_1dadb6f3);
  and and_15 (and_15_out, and_6_out, clock_1_out);
  not not_7 (not_7_out, WRITE_DATA_1dadb6f3);
  and and_16 (and_16_out, and_8_out, clock_1_out);
  not not_8 (not_8_out, WRITE_DATA_1dadb6f3);
  nand nand_17 (nand_17_out, WRITE_DATA_1dadb6f3, and_13_out);
  nand nand_18 (nand_18_out, and_13_out, not_5_out);
  nand nand_19 (nand_19_out, WRITE_DATA_1dadb6f3, and_14_out);
  nand nand_20 (nand_20_out, and_14_out, not_6_out);
  nand nand_21 (nand_21_out, WRITE_DATA_1dadb6f3, and_15_out);
  nand nand_22 (nand_22_out, and_15_out, not_7_out);
  nand nand_23 (nand_23_out, WRITE_DATA_1dadb6f3, and_16_out);
  nand nand_24 (nand_24_out, and_16_out, not_8_out);
  nand nand_25 (nand_25_out, nand_17_out, nand_26_out);
  nand nand_26 (nand_26_out, nand_25_out, nand_18_out);
  nand nand_27 (nand_27_out, nand_19_out, nand_28_out);
  nand nand_28 (nand_28_out, nand_27_out, nand_20_out);
  nand nand_29 (nand_29_out, nand_21_out, nand_30_out);
  nand nand_30 (nand_30_out, nand_29_out, nand_22_out);
  nand nand_31 (nand_31_out, nand_23_out, nand_32_out);
  nand nand_32 (nand_32_out, nand_31_out, nand_24_out);
  not not_9 (not_9_out, S2);
  not not_10 (not_10_out, S1);
  not not_11 (not_11_out, S1_2);
  not not_12 (not_12_out, S2_2);
  not not_13 (not_13_out, S0);
  not not_14 (not_14_out, S0_2);
  and and_17 (and_17_out, Enable_2, S2, S1, S0, nand_31_out);
  and and_18 (and_18_out, Enable_2, S2, S1, not_13_out, nand_15_out);
  and and_19 (and_19_out, Enable_2, S2, not_10_out, S0, nand_29_out);
  and and_20 (and_20_out, Enable_2, S2, not_10_out, not_13_out, nand_13_out);
  and and_21 (and_21_out, Enable_2, not_9_out, S1, S0, nand_27_out);
  and and_22 (and_22_out, Enable_2, not_9_out, S1, not_13_out, nand_11_out);
  and and_23 (and_23_out, Enable_2, not_9_out, not_10_out, S0, nand_25_out);
  and and_24 (and_24_out, Enable_2, not_9_out, not_10_out, not_13_out, nand_9_out);
  and and_25 (and_25_out, Enable_3, S2_2, S1_2, S0_2, nand_31_out);
  and and_26 (and_26_out, Enable_3, S2_2, S1_2, not_14_out, nand_15_out);
  and and_27 (and_27_out, Enable_3, S2_2, not_11_out, S0_2, nand_29_out);
  and and_28 (and_28_out, Enable_3, S2_2, not_11_out, not_14_out, nand_13_out);
  and and_29 (and_29_out, Enable_3, not_12_out, S1_2, S0_2, nand_27_out);
  and and_30 (and_30_out, Enable_3, not_12_out, S1_2, not_14_out, nand_11_out);
  and and_31 (and_31_out, Enable_3, not_12_out, not_11_out, S0_2, nand_25_out);
  and and_32 (and_32_out, Enable_3, not_12_out, not_11_out, not_14_out, nand_9_out);
  nor nor_1 (nor_1_out, and_17_out, and_18_out, and_19_out, and_20_out, and_21_out, and_22_out, and_23_out, and_24_out);
  nor nor_2 (nor_2_out, and_25_out, and_26_out, and_27_out, and_28_out, and_29_out, and_30_out, and_31_out, and_32_out);
  not not_15 (not_15_out, nor_1_out);
  not not_16 (not_16_out, nor_2_out);
  ExactlyOne xor_1 (.out(xor_1_out), .in0(not_16_out), .in3(in_14), .in4(in_14));
  xor xor_2 (xor_2_out, in_20, in_14);
  xor xor_3 (xor_3_out, in_26, in_14);
  xor xor_4 (xor_4_out, in_28, in_14);
  xor xor_5 (xor_5_out, in_30, in_14);
  xor xor_6 (xor_6_out, in_32, in_14);
  xor xor_7 (xor_7_out, in_34, in_14);
  xor xor_8 (xor_8_out, in_36, in_14);
  xor xor_9 (xor_9_out, in_38, in_14);
  xor xor_10 (xor_10_out, in_40, in_14);
  xor xor_11 (xor_11_out, in_42, in_14);
  xor xor_12 (xor_12_out, in_44, in_14);
  xor xor_13 (xor_13_out, in_46, in_14);
  xor xor_14 (xor_14_out, in_48, in_14);
  xor xor_15 (xor_15_out, in_50, in_14);
  xor xor_16 (xor_16_out, in_52, in_14);
  xor xor_17 (xor_17_out, not_15_out, xor_1_out);
  xor xor_18 (xor_18_out, in_19, xor_2_out);
  xor xor_19 (xor_19_out, in_25, xor_3_out);
  xor xor_20 (xor_20_out, in_27, xor_4_out);
  xor xor_21 (xor_21_out, in_29, xor_5_out);
  xor xor_22 (xor_22_out, in_31, xor_6_out);
  xor xor_23 (xor_23_out, in_33, xor_7_out);
  xor xor_24 (xor_24_out, in_35, xor_8_out);
  and and_33 (and_33_out, in_14, xor_17_out);
  and and_34 (and_34_out, xor_1_out, not_15_out);
  and and_35 (and_35_out, or_1_out, xor_18_out);
  and and_36 (and_36_out, xor_2_out, in_19);
  and and_37 (and_37_out, or_2_out, xor_19_out);
  and and_38 (and_38_out, xor_3_out, in_25);
  xor xor_25 (xor_25_out, in_37, xor_9_out);
  xor xor_26 (xor_26_out, in_39, xor_10_out);
  xor xor_27 (xor_27_out, in_41, xor_11_out);
  xor xor_28 (xor_28_out, in_43, xor_12_out);
  xor xor_29 (xor_29_out, xor_17_out, in_14);
  xor xor_30 (xor_30_out, xor_18_out, or_1_out);
  xor xor_31 (xor_31_out, xor_19_out, or_2_out);
  and and_39 (and_39_out, or_3_out, xor_20_out);
  and and_40 (and_40_out, xor_4_out, in_27);
  and and_41 (and_41_out, or_5_out, xor_21_out);
  and and_42 (and_42_out, xor_5_out, in_29);
  and and_43 (and_43_out, or_4_out, xor_22_out);
  and and_44 (and_44_out, xor_6_out, in_31);
  and and_45 (and_45_out, or_6_out, xor_23_out);
  and and_46 (and_46_out, xor_7_out, in_33);
  and and_47 (and_47_out, or_7_out, xor_24_out);
  and and_48 (and_48_out, xor_8_out, in_35);
  and and_49 (and_49_out, or_8_out, xor_25_out);
  and and_50 (and_50_out, xor_9_out, in_37);
  xor xor_32 (xor_32_out, in_45, xor_13_out);
  xor xor_33 (xor_33_out, in_47, xor_14_out);
  xor xor_34 (xor_34_out, in_49, xor_15_out);
  xor xor_35 (xor_35_out, in_51, xor_16_out);
  or or_1 (or_1_out, and_33_out, and_34_out);
  or or_2 (or_2_out, and_35_out, and_36_out);
  or or_3 (or_3_out, and_37_out, and_38_out);
  xor xor_36 (xor_36_out, xor_20_out, or_3_out);
  xor xor_37 (xor_37_out, xor_21_out, or_5_out);
  or or_4 (or_4_out, and_41_out, and_42_out);
  xor xor_38 (xor_38_out, xor_22_out, or_4_out);
  xor xor_39 (xor_39_out, xor_23_out, or_6_out);
  xor xor_40 (xor_40_out, xor_24_out, or_7_out);
  xor xor_41 (xor_41_out, xor_25_out, or_8_out);
  xor xor_42 (xor_42_out, xor_26_out, or_9_out);
  and and_51 (and_51_out, or_9_out, xor_26_out);
  and and_52 (and_52_out, xor_10_out, in_39);
  and and_53 (and_53_out, or_10_out, xor_27_out);
  and and_54 (and_54_out, xor_11_out, in_41);
  and and_55 (and_55_out, or_11_out, xor_28_out);
  and and_56 (and_56_out, xor_12_out, in_43);
  and and_57 (and_57_out, or_12_out, xor_32_out);
  and and_58 (and_58_out, xor_13_out, in_45);
  or or_5 (or_5_out, and_39_out, and_40_out);
  or or_6 (or_6_out, and_43_out, and_44_out);
  or or_7 (or_7_out, and_45_out, and_46_out);
  or or_8 (or_8_out, and_47_out, and_48_out);
  or or_9 (or_9_out, and_49_out, and_50_out);
  or or_10 (or_10_out, and_51_out, and_52_out);
  xor xor_43 (xor_43_out, xor_27_out, or_10_out);
  or or_11 (or_11_out, and_53_out, and_54_out);
  xor xor_44 (xor_44_out, xor_28_out, or_11_out);
  xor xor_45 (xor_45_out, xor_32_out, or_12_out);
  xor xor_46 (xor_46_out, xor_33_out, or_13_out);
  and and_59 (and_59_out, or_13_out, xor_33_out);
  and and_60 (and_60_out, xor_14_out, in_47);
  xor xor_47 (xor_47_out, xor_34_out, or_14_out);
  and and_61 (and_61_out, or_14_out, xor_34_out);
  and and_62 (and_62_out, xor_15_out, in_49);
  xor xor_48 (xor_48_out, xor_35_out, or_15_out);
  and and_63 (and_63_out, or_15_out, xor_35_out);
  and and_64 (and_64_out, xor_16_out, in_51);
  or or_12 (or_12_out, and_55_out, and_56_out);
  or or_13 (or_13_out, and_57_out, and_58_out);
  or or_14 (or_14_out, and_59_out, and_60_out);
  or or_15 (or_15_out, and_61_out, and_62_out);
  or or_16 (or_16_out, and_63_out, and_64_out);
  not not_17 (not_17_out, not_15_out);
  and and_65 (and_65_out, not_16_out, not_15_out);
  or or_17 (or_17_out, not_15_out, not_16_out);
  xor xor_49 (xor_49_out, not_15_out, not_16_out);
  nand nand_33 (nand_33_out, not_16_out, not_15_out);
  nor nor_3 (nor_3_out, not_15_out, not_16_out);
  not not_18 (not_18_out, in_19);
  and and_66 (and_66_out, in_20, in_19);
  or or_18 (or_18_out, in_19, in_20);
  xor xor_50 (xor_50_out, in_19, in_20);
  nand nand_34 (nand_34_out, in_20, in_19);
  nor nor_4 (nor_4_out, in_19, in_20);
  not not_19 (not_19_out, in_25);
  and and_67 (and_67_out, in_26, in_25);
  or or_19 (or_19_out, in_25, in_26);
  xor xor_51 (xor_51_out, in_25, in_26);
  nand nand_35 (nand_35_out, in_26, in_25);
  nor nor_5 (nor_5_out, in_25, in_26);
  not not_20 (not_20_out, in_27);
  not not_21 (not_21_out, in_29);
  and and_68 (and_68_out, in_28, in_27);
  or or_20 (or_20_out, in_27, in_28);
  xor xor_52 (xor_52_out, in_27, in_28);
  nand nand_36 (nand_36_out, in_28, in_27);
  nor nor_6 (nor_6_out, in_27, in_28);
  and and_69 (and_69_out, in_30, in_29);
  or or_21 (or_21_out, in_29, in_30);
  xor xor_53 (xor_53_out, in_29, in_30);
  nand nand_37 (nand_37_out, in_30, in_29);
  nor nor_7 (nor_7_out, in_29, in_30);
  not not_22 (not_22_out, in_31);
  and and_70 (and_70_out, in_32, in_31);
  or or_22 (or_22_out, in_31, in_32);
  xor xor_54 (xor_54_out, in_31, in_32);
  nand nand_38 (nand_38_out, in_32, in_31);
  nor nor_8 (nor_8_out, in_31, in_32);
  not not_23 (not_23_out, in_33);
  and and_71 (and_71_out, in_34, in_33);
  or or_23 (or_23_out, in_33, in_34);
  xor xor_55 (xor_55_out, in_33, in_34);
  nand nand_39 (nand_39_out, in_34, in_33);
  nor nor_9 (nor_9_out, in_33, in_34);
  not not_24 (not_24_out, in_35);
  and and_72 (and_72_out, in_36, in_35);
  or or_24 (or_24_out, in_35, in_36);
  xor xor_56 (xor_56_out, in_35, in_36);
  nand nand_40 (nand_40_out, in_36, in_35);
  nor nor_10 (nor_10_out, in_35, in_36);
  not not_25 (not_25_out, in_37);
  and and_73 (and_73_out, in_38, in_37);
  or or_25 (or_25_out, in_37, in_38);
  xor xor_57 (xor_57_out, in_37, in_38);
  nand nand_41 (nand_41_out, in_38, in_37);
  nor nor_11 (nor_11_out, in_37, in_38);
  not not_26 (not_26_out, in_39);
  and and_74 (and_74_out, in_40, in_39);
  or or_26 (or_26_out, in_39, in_40);
  xor xor_58 (xor_58_out, in_39, in_40);
  nand nand_42 (nand_42_out, in_40, in_39);
  nor nor_12 (nor_12_out, in_39, in_40);
  not not_27 (not_27_out, in_41);
  and and_75 (and_75_out, in_42, in_41);
  or or_27 (or_27_out, in_41, in_42);
  xor xor_59 (xor_59_out, in_41, in_42);
  nand nand_43 (nand_43_out, in_42, in_41);
  nor nor_13 (nor_13_out, in_41, in_42);
  not not_28 (not_28_out, in_43);
  and and_76 (and_76_out, in_44, in_43);
  or or_28 (or_28_out, in_43, in_44);
  xor xor_60 (xor_60_out, in_43, in_44);
  nand nand_44 (nand_44_out, in_44, in_43);
  nor nor_14 (nor_14_out, in_43, in_44);
  not not_29 (not_29_out, in_45);
  and and_77 (and_77_out, in_46, in_45);
  or or_29 (or_29_out, in_45, in_46);
  xor xor_61 (xor_61_out, in_45, in_46);
  nand nand_45 (nand_45_out, in_46, in_45);
  nor nor_15 (nor_15_out, in_45, in_46);
  not not_30 (not_30_out, in_47);
  and and_78 (and_78_out, in_48, in_47);
  or or_30 (or_30_out, in_47, in_48);
  not not_31 (not_31_out, in_49);
  and and_79 (and_79_out, in_50, in_49);
  or or_31 (or_31_out, in_49, in_50);
  not not_32 (not_32_out, in_51);
  and and_80 (and_80_out, in_52, in_51);
  or or_32 (or_32_out, in_51, in_52);
  xor xor_62 (xor_62_out, in_47, in_48);
  nand nand_46 (nand_46_out, in_48, in_47);
  nor nor_16 (nor_16_out, in_47, in_48);
  xor xor_63 (xor_63_out, in_49, in_50);
  nand nand_47 (nand_47_out, in_50, in_49);
  nor nor_17 (nor_17_out, in_49, in_50);
  xor xor_64 (xor_64_out, in_51, in_52);
  nand nand_48 (nand_48_out, in_52, in_51);
  nor nor_18 (nor_18_out, in_51, in_52);
  not not_33 (not_33_out, in_11);
  not not_34 (not_34_out, in_12);
  not not_35 (not_35_out, in_13);
  and and_81 (and_81_out, in_14, not_33_out, not_34_out, not_35_out);
  and and_82 (and_82_out, xor_29_out, not_33_out, not_34_out, in_13);
  and and_83 (and_83_out, not_17_out, in_12, not_33_out, not_35_out);
  and and_84 (and_84_out, and_65_out, in_13, in_12, not_33_out);
  and and_85 (and_85_out, or_17_out, not_35_out, not_34_out, in_11);
  and and_86 (and_86_out, xor_49_out, in_13, in_11, not_34_out);
  and and_87 (and_87_out, nand_33_out, not_35_out, in_11, in_12);
  and and_88 (and_88_out, nor_3_out, in_13, in_12, in_11);
  and and_89 (and_89_out, in_14, not_33_out, not_34_out, not_35_out);
  and and_90 (and_90_out, xor_30_out, not_33_out, not_34_out, in_13);
  and and_91 (and_91_out, not_18_out, in_12, not_33_out, not_35_out);
  and and_92 (and_92_out, and_66_out, in_13, in_12, not_33_out);
  and and_93 (and_93_out, or_18_out, not_35_out, not_34_out, in_11);
  and and_94 (and_94_out, xor_50_out, in_13, in_11, not_34_out);
  and and_95 (and_95_out, nand_34_out, not_35_out, in_11, in_12);
  and and_96 (and_96_out, nor_4_out, in_13, in_12, in_11);
  and and_97 (and_97_out, in_14, not_33_out, not_34_out, not_35_out);
  and and_98 (and_98_out, xor_31_out, not_33_out, not_34_out, in_13);
  and and_99 (and_99_out, not_19_out, in_12, not_33_out, not_35_out);
  and and_100 (and_100_out, and_67_out, in_13, in_12, not_33_out);
  and and_101 (and_101_out, or_19_out, not_35_out, not_34_out, in_11);
  and and_102 (and_102_out, xor_51_out, in_13, in_11, not_34_out);
  and and_103 (and_103_out, nand_35_out, not_35_out, in_11, in_12);
  and and_104 (and_104_out, nor_5_out, in_13, in_12, in_11);
  and and_105 (and_105_out, in_14, not_33_out, not_34_out, not_35_out);
  and and_106 (and_106_out, xor_36_out, not_33_out, not_34_out, in_13);
  and and_107 (and_107_out, not_20_out, in_12, not_33_out, not_35_out);
  and and_108 (and_108_out, and_68_out, in_13, in_12, not_33_out);
  and and_109 (and_109_out, or_20_out, not_35_out, not_34_out, in_11);
  and and_110 (and_110_out, xor_52_out, in_13, in_11, not_34_out);
  and and_111 (and_111_out, nand_36_out, not_35_out, in_11, in_12);
  and and_112 (and_112_out, nor_6_out, in_13, in_12, in_11);
  and and_113 (and_113_out, in_14, not_33_out, not_34_out, not_35_out);
  and and_114 (and_114_out, xor_37_out, not_33_out, not_34_out, in_13);
  and and_115 (and_115_out, not_21_out, in_12, not_33_out, not_35_out);
  and and_116 (and_116_out, and_69_out, in_13, in_12, not_33_out);
  and and_117 (and_117_out, or_21_out, not_35_out, not_34_out, in_11);
  and and_118 (and_118_out, xor_53_out, in_13, in_11, not_34_out);
  and and_119 (and_119_out, nand_37_out, not_35_out, in_11, in_12);
  and and_120 (and_120_out, nor_7_out, in_13, in_12, in_11);
  and and_121 (and_121_out, in_14, not_33_out, not_34_out, not_35_out);
  and and_122 (and_122_out, xor_38_out, not_33_out, not_34_out, in_13);
  and and_123 (and_123_out, not_22_out, in_12, not_33_out, not_35_out);
  and and_124 (and_124_out, and_70_out, in_13, in_12, not_33_out);
  and and_125 (and_125_out, or_22_out, not_35_out, not_34_out, in_11);
  and and_126 (and_126_out, xor_54_out, in_13, in_11, not_34_out);
  and and_127 (and_127_out, nand_38_out, not_35_out, in_11, in_12);
  and and_128 (and_128_out, nor_8_out, in_13, in_12, in_11);
  and and_129 (and_129_out, in_14, not_33_out, not_34_out, not_35_out);
  and and_130 (and_130_out, xor_39_out, not_33_out, not_34_out, in_13);
  and and_131 (and_131_out, not_23_out, in_12, not_33_out, not_35_out);
  and and_132 (and_132_out, and_71_out, in_13, in_12, not_33_out);
  and and_133 (and_133_out, or_23_out, not_35_out, not_34_out, in_11);
  and and_134 (and_134_out, xor_55_out, in_13, in_11, not_34_out);
  and and_135 (and_135_out, nand_39_out, not_35_out, in_11, in_12);
  and and_136 (and_136_out, nor_9_out, in_13, in_12, in_11);
  and and_137 (and_137_out, in_14, not_33_out, not_34_out, not_35_out);
  and and_138 (and_138_out, xor_40_out, not_33_out, not_34_out, in_13);
  and and_139 (and_139_out, not_24_out, in_12, not_33_out, not_35_out);
  and and_140 (and_140_out, and_72_out, in_13, in_12, not_33_out);
  and and_141 (and_141_out, or_24_out, not_35_out, not_34_out, in_11);
  and and_142 (and_142_out, xor_56_out, in_13, in_11, not_34_out);
  and and_143 (and_143_out, nand_40_out, not_35_out, in_11, in_12);
  and and_144 (and_144_out, nor_10_out, in_13, in_12, in_11);
  and and_145 (and_145_out, in_14, not_33_out, not_34_out, not_35_out);
  and and_146 (and_146_out, xor_41_out, not_33_out, not_34_out, in_13);
  and and_147 (and_147_out, not_25_out, in_12, not_33_out, not_35_out);
  and and_148 (and_148_out, and_73_out, in_13, in_12, not_33_out);
  and and_149 (and_149_out, or_25_out, not_35_out, not_34_out, in_11);
  and and_150 (and_150_out, xor_57_out, in_13, in_11, not_34_out);
  and and_151 (and_151_out, nand_41_out, not_35_out, in_11, in_12);
  and and_152 (and_152_out, nor_11_out, in_13, in_12, in_11);
  and and_153 (and_153_out, in_14, not_33_out, not_34_out, not_35_out);
  and and_154 (and_154_out, xor_42_out, not_33_out, not_34_out, in_13);
  and and_155 (and_155_out, not_26_out, in_12, not_33_out, not_35_out);
  and and_156 (and_156_out, and_74_out, in_13, in_12, not_33_out);
  and and_157 (and_157_out, or_26_out, not_35_out, not_34_out, in_11);
  and and_158 (and_158_out, xor_58_out, in_13, in_11, not_34_out);
  and and_159 (and_159_out, nand_42_out, not_35_out, in_11, in_12);
  and and_160 (and_160_out, nor_12_out, in_13, in_12, in_11);
  and and_161 (and_161_out, in_14, not_33_out, not_34_out, not_35_out);
  and and_162 (and_162_out, xor_43_out, not_33_out, not_34_out, in_13);
  and and_163 (and_163_out, not_27_out, in_12, not_33_out, not_35_out);
  and and_164 (and_164_out, and_75_out, in_13, in_12, not_33_out);
  and and_165 (and_165_out, or_27_out, not_35_out, not_34_out, in_11);
  and and_166 (and_166_out, xor_59_out, in_13, in_11, not_34_out);
  and and_167 (and_167_out, nand_43_out, not_35_out, in_11, in_12);
  and and_168 (and_168_out, nor_13_out, in_13, in_12, in_11);
  and and_169 (and_169_out, in_14, not_33_out, not_34_out, not_35_out);
  and and_170 (and_170_out, xor_44_out, not_33_out, not_34_out, in_13);
  and and_171 (and_171_out, not_28_out, in_12, not_33_out, not_35_out);
  and and_172 (and_172_out, and_76_out, in_13, in_12, not_33_out);
  and and_173 (and_173_out, or_28_out, not_35_out, not_34_out, in_11);
  and and_174 (and_174_out, xor_60_out, in_13, in_11, not_34_out);
  and and_175 (and_175_out, nand_44_out, not_35_out, in_11, in_12);
  and and_176 (and_176_out, nor_14_out, in_13, in_12, in_11);
  and and_177 (and_177_out, in_14, not_33_out, not_34_out, not_35_out);
  and and_178 (and_178_out, xor_45_out, not_33_out, not_34_out, in_13);
  and and_179 (and_179_out, not_29_out, in_12, not_33_out, not_35_out);
  and and_180 (and_180_out, and_77_out, in_13, in_12, not_33_out);
  and and_181 (and_181_out, or_29_out, not_35_out, not_34_out, in_11);
  and and_182 (and_182_out, xor_61_out, in_13, in_11, not_34_out);
  and and_183 (and_183_out, nand_45_out, not_35_out, in_11, in_12);
  and and_184 (and_184_out, nor_15_out, in_13, in_12, in_11);
  and and_185 (and_185_out, in_14, not_33_out, not_34_out, not_35_out);
  and and_186 (and_186_out, xor_46_out, not_33_out, not_34_out, in_13);
  and and_187 (and_187_out, not_30_out, in_12, not_33_out, not_35_out);
  and and_188 (and_188_out, and_78_out, in_13, in_12, not_33_out);
  and and_189 (and_189_out, or_30_out, not_35_out, not_34_out, in_11);
  and and_190 (and_190_out, xor_62_out, in_13, in_11, not_34_out);
  and and_191 (and_191_out, nand_46_out, not_35_out, in_11, in_12);
  and and_192 (and_192_out, nor_16_out, in_13, in_12, in_11);
  and and_193 (and_193_out, in_14, not_33_out, not_34_out, not_35_out);
  and and_194 (and_194_out, xor_47_out, not_33_out, not_34_out, in_13);
  and and_195 (and_195_out, not_31_out, in_12, not_33_out, not_35_out);
  and and_196 (and_196_out, and_79_out, in_13, in_12, not_33_out);
  and and_197 (and_197_out, or_31_out, not_35_out, not_34_out, in_11);
  and and_198 (and_198_out, xor_63_out, in_13, in_11, not_34_out);
  and and_199 (and_199_out, nand_47_out, not_35_out, in_11, in_12);
  and and_200 (and_200_out, nor_17_out, in_13, in_12, in_11);
  and and_201 (and_201_out, in_14, not_33_out, not_34_out, not_35_out);
  and and_202 (and_202_out, xor_48_out, not_33_out, not_34_out, in_13);
  and and_203 (and_203_out, not_32_out, in_12, not_33_out, not_35_out);
  and and_204 (and_204_out, and_80_out, in_13, in_12, not_33_out);
  and and_205 (and_205_out, or_32_out, not_35_out, not_34_out, in_11);
  and and_206 (and_206_out, xor_64_out, in_13, in_11, not_34_out);
  and and_207 (and_207_out, nand_48_out, not_35_out, in_11, in_12);
  and and_208 (and_208_out, nor_18_out, in_13, in_12, in_11);
  or or_33 (or_33_out, and_81_out, and_82_out, and_83_out, and_84_out, and_85_out, and_86_out, and_87_out, and_88_out);
  or or_34 (or_34_out, and_89_out, and_90_out, and_91_out, and_92_out, and_93_out, and_94_out, and_95_out, and_96_out);
  or or_35 (or_35_out, and_97_out, and_98_out, and_99_out, and_100_out, and_101_out, and_102_out, and_103_out, and_104_out);
  or or_36 (or_36_out, and_105_out, and_106_out, and_107_out, and_108_out, and_109_out, and_110_out, and_111_out, and_112_out);
  or or_37 (or_37_out, and_113_out, and_114_out, and_115_out, and_116_out, and_117_out, and_118_out, and_119_out, and_120_out);
  or or_38 (or_38_out, and_121_out, and_122_out, and_123_out, and_124_out, and_125_out, and_126_out, and_127_out, and_128_out);
  or or_39 (or_39_out, and_129_out, and_130_out, and_131_out, and_132_out, and_133_out, and_134_out, and_135_out, and_136_out);
  or or_40 (or_40_out, and_137_out, and_138_out, and_139_out, and_140_out, and_141_out, and_142_out, and_143_out, and_144_out);
  or or_41 (or_41_out, and_145_out, and_146_out, and_147_out, and_148_out, and_149_out, and_150_out, and_151_out, and_152_out);
  or or_42 (or_42_out, and_153_out, and_154_out, and_155_out, and_156_out, and_157_out, and_158_out, and_159_out, and_160_out);
  or or_43 (or_43_out, and_161_out, and_162_out, and_163_out, and_164_out, and_165_out, and_166_out, and_167_out, and_168_out);
  or or_44 (or_44_out, and_169_out, and_170_out, and_171_out, and_172_out, and_173_out, and_174_out, and_175_out, and_176_out);
  or or_45 (or_45_out, and_177_out, and_178_out, and_179_out, and_180_out, and_181_out, and_182_out, and_183_out, and_184_out);
  or or_46 (or_46_out, and_185_out, and_186_out, and_187_out, and_188_out, and_189_out, and_190_out, and_191_out, and_192_out);
  or or_47 (or_47_out, and_193_out, and_194_out, and_195_out, and_196_out, and_197_out, and_198_out, and_199_out, and_200_out);
  or or_48 (or_48_out, and_201_out, and_202_out, and_203_out, and_204_out, and_205_out, and_206_out, and_207_out, and_208_out);
  LED led_1 (.in(or_33_out));
  LED led_2 (.in(or_34_out));
  LED led_3 (.in(or_35_out));
  LED led_4 (.in(or_36_out));
  LED led_5 (.in(or_37_out));
  LED led_6 (.in(or_38_out));
  LED led_7 (.in(or_39_out));
  LED led_8 (.in(or_40_out));
  LED led_9 (.in(or_41_out));
  LED led_10 (.in(or_42_out));
  LED led_11 (.in(or_43_out));
  LED led_12 (.in(or_44_out));
  LED led_13 (.in(or_45_out));
  LED led_14 (.in(or_46_out));
  LED led_15 (.in(or_47_out));
  LED led_16 (.in(or_48_out));

  // Notes on the sheet:
  //   R0
  //   R4
  //   R6
  //   R2
  //   R1
  //   R3
  //   R5
  //   R7
  //   D7
  //   D6
  //   D5
  //   D4
  //   D3
  //   D2
  //   D1
  //   D0
  //   X1
  //   \X1
  //   X2
  //   \X2
endmodule
